// Logisim project laboratorio.circ as structural Verilog: 2 circuits, main circuit main
module main (
  input  in_1,
  input  in_2,
  input  in_3,
  input  in_4
);

  wire display_circ_1_a, display_circ_1_b, display_circ_1_c, display_circ_1_d, display_circ_1_out_9,
       display_circ_1_out_10, display_circ_1_out_11;

  display_circ display_circ_1 (
    .in_1(in_1), .in_2(in_2), .in_3(in_3), .in_4(in_4), .a(display_circ_1_a), .b(display_circ_1_b),
    .c(display_circ_1_c), .d(display_circ_1_d), .out_9(display_circ_1_out_9), .out_10(display_circ_1_out_10),
    .out_11(display_circ_1_out_11));
  _7_Segment_Display u_7_segment_display_1 (
    .g(display_circ_1_out_11), .f(display_circ_1_out_10), .a(display_circ_1_a), .b(display_circ_1_b),
    .e(display_circ_1_out_9), .d(display_circ_1_d), .c(display_circ_1_c));  // open: dp

  // Notes on the sheet:
  //   display.circ
endmodule

module display_circ (
  input  in_1,
  input  in_2,
  input  in_3,
  input  in_4,
  output a,
  output b,
  output c,
  output d,
  output out_9,
  output out_10,
  output out_11
);

  wire and_1_out, and_2_out, and_3_out, and_4_out, and_5_out, and_6_out, and_7_out, and_8_out, and_9_out,
       and_10_out, and_11_out, and_12_out, and_13_out, and_14_out, and_15_out, and_16_out, and_17_out,
       and_18_out, and_19_out, and_20_out, and_21_out, and_22_out, and_23_out, and_24_out, and_25_out,
       and_26_out, and_27_out, and_28_out, and_29_out, not_1_out, not_2_out, not_3_out, not_4_out, or_2_out,
       or_3_out;

  not not_1 (not_1_out, in_1);
  not not_2 (not_2_out, in_2);
  not not_3 (not_3_out, in_3);
  not not_4 (not_4_out, in_4);
  and and_1 (and_1_out, in_2, not_1_out);
  and and_2 (and_2_out, in_4, in_3);
  and and_3 (and_3_out, in_3, not_2_out);
  and and_4 (and_4_out, not_4_out, not_2_out, not_1_out);
  and and_5 (and_5_out, not_3_out, not_2_out, not_1_out);
  and and_6 (and_6_out, in_4, not_3_out, not_2_out);
  and and_7 (and_7_out, not_4_out, in_2, in_1);
  and and_8 (and_8_out, in_3, in_2, in_1);
  and and_9 (and_9_out, in_4, in_3, in_2);
  and and_10 (and_10_out, not_3_out, not_2_out);
  and and_11 (and_11_out, not_4_out, not_3_out, in_1);
  and and_12 (and_12_out, not_4_out, in_3, in_2);
  and and_13 (and_13_out, in_4, in_2, not_1_out);
  and and_14 (and_14_out, in_4, in_3, not_2_out);
  and and_15 (and_15_out, not_4_out, in_2, not_1_out);
  and and_16 (and_16_out, not_4_out, not_3_out, in_2);
  and and_17 (and_17_out, in_3, in_2, not_1_out);
  and and_18 (and_18_out, not_4_out, not_3_out, in_1);
  and and_19 (and_19_out, in_4, not_3_out, in_1);
  and and_20 (and_20_out, not_4_out, in_3, not_2_out, not_1_out);
  or or_1 (out_9, not_4_out, in_3, in_2, in_1);
  and and_21 (and_21_out, in_4, in_2);
  and and_22 (and_22_out, not_4_out, in_3);
  and and_23 (and_23_out, not_4_out, not_3_out, not_2_out);
  and and_24 (and_24_out, in_2, not_1_out);
  and and_25 (and_25_out, not_4_out, not_2_out);
  and and_26 (and_26_out, not_4_out, in_2, in_1);
  and and_27 (and_27_out, in_3, not_2_out, not_1_out);
  and and_28 (and_28_out, in_3, in_2, in_1);
  and and_29 (and_29_out, in_4, not_3_out, in_2, not_1_out);
  or or_2 (or_2_out, and_15_out, and_16_out, and_17_out);
  or or_3 (or_3_out, and_18_out, and_19_out, and_20_out);
  or or_4 (out_10, and_21_out, and_22_out, and_23_out, and_24_out);
  or or_5 (out_11, and_25_out, and_26_out, and_27_out, and_28_out, and_29_out);
  or or_6 (a, and_1_out, and_2_out, and_3_out, and_4_out);
  or or_7 (b, and_5_out, and_6_out, and_7_out, and_8_out, and_9_out);
  or or_8 (c, and_10_out, and_11_out, and_12_out, and_13_out, and_14_out);
  or or_9 (d, or_2_out, or_3_out);

  // Notes on the sheet:
  //   a
  //   b
  //   e
  //   f
  //   g
endmodule
