// Logisim project mapa.circ as structural Verilog: 6 circuits, main circuit main
module main (
  input  [3:0] Input_Usuario,
  input  LOAD
);

  wire CLK_out, D7_a, D7_b, D7_c, D7_d, D7_out_6, D7_out_7, D7_out_8, DetectF_isf, not_1_out, not_2_out,
       R_out;
  wire [3:0] Mux_de_carga_state__4_bit, NextState__4_bit_output, StateRegister_q_3__0__currentstate;

  Button R (.out(R_out));
  not not_1 (not_1_out, LOAD);
  mux_de_carga Mux_de_carga (
    .UserIn(Input_Usuario), .NextState(NextState__4_bit_output), .LOAD(not_1_out),
    .State__4_bit(Mux_de_carga_state__4_bit));
  NextState NextState (._4_bit_Input(StateRegister_q_3__0__currentstate), ._4_bit_Output(NextState__4_bit_output));
  Clock CLK (.out(CLK_out));
  not not_2 (not_2_out, DetectF_isf);
  LED Finished (.in(DetectF_isf));
  DetectF DetectF (.CurrentState(StateRegister_q_3__0__currentstate), .IsF(DetectF_isf));
  StateRegister StateRegister (
    .CLK(CLK_out), .D_3__0(Mux_de_carga_state__4_bit), .LOAD(not_2_out), .Reset(R_out),
    .Q_3__0__CurrentState(StateRegister_q_3__0__currentstate));
  D7 D7 (
    .in_1(StateRegister_q_3__0__currentstate), .a(D7_a), .b(D7_b), .c(D7_c), .d(D7_d), .out_6(D7_out_6),
    .out_7(D7_out_7), .out_8(D7_out_8));
  _7_Segment_Display u_7_segment_display_1 (
    .g(D7_out_8), .f(D7_out_7), .a(D7_a), .b(D7_b), .e(D7_out_6), .d(D7_d), .c(D7_c));  // open: dp

  // Notes on the sheet:
  //   Reset
endmodule

module mux_de_carga (
  input  [3:0] UserIn,
  input  [3:0] NextState,
  input  LOAD,
  output [3:0] State__4_bit
);

  Multiplexer #(.enable("false")) multiplexer_1 (
    .in0(UserIn[0]), .in1(NextState[0]), .out(State__4_bit[0]), .sel(LOAD));
  Multiplexer #(.enable("false")) multiplexer_2 (
    .in0(UserIn[1]), .in1(NextState[1]), .out(State__4_bit[1]), .sel(LOAD));
  Multiplexer #(.enable("false")) multiplexer_3 (
    .in0(UserIn[2]), .in1(NextState[2]), .out(State__4_bit[2]), .sel(LOAD));
  Multiplexer #(.enable("false")) multiplexer_4 (
    .in0(UserIn[3]), .in1(NextState[3]), .out(State__4_bit[3]), .sel(LOAD));
endmodule

module NextState (
  input  [3:0] _4_bit_Input,
  output [3:0] _4_bit_Output
);

  wire and_1_out, and_2_out, and_3_out, and_4_out, and_5_out, and_6_out, and_7_out, and_8_out, and_9_out,
       and_10_out, and_11_out, and_12_out, and_13_out, and_14_out, and_15_out, and_16_out, not_1_out,
       not_2_out, not_3_out, not_4_out;

  not not_1 (not_1_out, _4_bit_Input[1]);
  not not_2 (not_2_out, _4_bit_Input[3]);
  not not_3 (not_3_out, _4_bit_Input[0]);
  not not_4 (not_4_out, _4_bit_Input[2]);
  and and_1 (and_1_out, _4_bit_Input[3], not_4_out);
  and and_2 (and_2_out, _4_bit_Input[3], not_1_out);
  and and_3 (and_3_out, not_2_out, _4_bit_Input[1], _4_bit_Input[0]);
  and and_4 (and_4_out, _4_bit_Input[3], _4_bit_Input[2]);
  and and_5 (and_5_out, _4_bit_Input[1], _4_bit_Input[2]);
  and and_6 (and_6_out, _4_bit_Input[1], _4_bit_Input[3]);
  and and_7 (and_7_out, _4_bit_Input[0], _4_bit_Input[2]);
  and and_8 (and_8_out, _4_bit_Input[0], _4_bit_Input[3]);
  and and_9 (and_9_out, not_2_out, _4_bit_Input[2], not_3_out);
  and and_10 (and_10_out, _4_bit_Input[3], _4_bit_Input[2], not_1_out);
  and and_11 (and_11_out, not_2_out, not_4_out, not_1_out, _4_bit_Input[0]);
  and and_12 (and_12_out, not_2_out, not_1_out);
  and and_13 (and_13_out, not_2_out, not_3_out);
  and and_14 (and_14_out, _4_bit_Input[3], _4_bit_Input[1]);
  and and_15 (and_15_out, not_4_out, not_3_out);
  and and_16 (and_16_out, _4_bit_Input[3], _4_bit_Input[2], _4_bit_Input[0]);
  or or_1 (_4_bit_Output[3], and_1_out, and_2_out, and_3_out);
  or or_2 (_4_bit_Output[2], and_4_out, and_5_out, and_6_out, and_7_out, and_8_out);
  or or_3 (_4_bit_Output[1], and_9_out, and_10_out, and_11_out);
  or or_4 (_4_bit_Output[0], and_12_out, and_13_out, and_14_out, and_15_out, and_16_out);
endmodule

module DetectF (
  input  [3:0] CurrentState,
  output IsF
);

  wire not_1_out, not_2_out;

  not not_1 (not_1_out, CurrentState[1]);
  not not_2 (not_2_out, CurrentState[3]);
  and and_1 (IsF, CurrentState[0], not_1_out, CurrentState[2], not_2_out);
endmodule

module StateRegister (
  input  CLK,
  input  [3:0] D_3__0,
  input  LOAD,
  input  Reset,
  output [3:0] Q_3__0__CurrentState
);

  D_Flip_Flop d_ff_1 (
    .clk(CLK), .D(D_3__0[0]), .Q(Q_3__0__CurrentState[0]), .en(LOAD), .reset(Reset));  // open: Qn, preset
  D_Flip_Flop d_ff_2 (
    .clk(CLK), .D(D_3__0[1]), .Q(Q_3__0__CurrentState[1]), .en(LOAD), .reset(Reset));  // open: Qn, preset
  D_Flip_Flop d_ff_3 (
    .clk(CLK), .D(D_3__0[2]), .Q(Q_3__0__CurrentState[2]), .en(LOAD), .reset(Reset));  // open: Qn, preset
  D_Flip_Flop d_ff_4 (
    .clk(CLK), .D(D_3__0[3]), .Q(Q_3__0__CurrentState[3]), .en(LOAD), .reset(Reset));  // open: Qn, preset
endmodule

module D7 (
  input  [3:0] in_1,
  output a,
  output b,
  output c,
  output d,
  output out_6,
  output out_7,
  output out_8
);

  wire and_1_out, and_2_out, and_3_out, and_4_out, and_5_out, and_6_out, and_7_out, and_8_out, and_9_out,
       and_10_out, and_11_out, and_12_out, and_13_out, and_14_out, and_15_out, and_16_out, and_17_out,
       and_18_out, and_19_out, and_20_out, and_21_out, and_22_out, and_23_out, and_24_out, and_25_out,
       and_26_out, and_27_out, and_28_out, and_29_out, not_1_out, not_2_out, not_3_out, not_4_out, or_5_out,
       or_7_out;

  not not_1 (not_1_out, in_1[0]);
  not not_2 (not_2_out, in_1[1]);
  not not_3 (not_3_out, in_1[2]);
  not not_4 (not_4_out, in_1[3]);
  and and_1 (and_1_out, in_1[1], not_1_out);
  and and_2 (and_2_out, in_1[3], in_1[2]);
  and and_3 (and_3_out, in_1[2], not_2_out);
  and and_4 (and_4_out, not_4_out, not_2_out, not_1_out);
  and and_5 (and_5_out, not_3_out, not_2_out, not_1_out);
  and and_6 (and_6_out, in_1[3], not_3_out, not_2_out);
  and and_7 (and_7_out, not_4_out, in_1[1], in_1[0]);
  and and_8 (and_8_out, in_1[2], in_1[1], in_1[0]);
  and and_9 (and_9_out, in_1[3], in_1[2], in_1[1]);
  and and_10 (and_10_out, not_3_out, not_2_out);
  and and_11 (and_11_out, not_4_out, not_3_out, in_1[0]);
  and and_12 (and_12_out, not_4_out, in_1[2], in_1[1]);
  and and_13 (and_13_out, in_1[3], in_1[1], not_1_out);
  and and_14 (and_14_out, in_1[3], in_1[2], not_2_out);
  and and_15 (and_15_out, not_4_out, in_1[1], not_1_out);
  and and_16 (and_16_out, not_4_out, not_3_out, in_1[1]);
  and and_17 (and_17_out, in_1[2], in_1[1], not_1_out);
  and and_18 (and_18_out, not_4_out, not_3_out, in_1[0]);
  and and_19 (and_19_out, in_1[3], not_3_out, in_1[0]);
  and and_20 (and_20_out, not_4_out, in_1[2], not_2_out, not_1_out);
  or or_1 (out_6, not_4_out, in_1[2], in_1[1], in_1[0]);
  and and_21 (and_21_out, in_1[3], in_1[1]);
  and and_22 (and_22_out, not_4_out, in_1[2]);
  and and_23 (and_23_out, not_4_out, not_3_out, not_2_out);
  and and_24 (and_24_out, in_1[1], not_1_out);
  and and_25 (and_25_out, not_4_out, not_2_out);
  and and_26 (and_26_out, not_4_out, in_1[1], in_1[0]);
  and and_27 (and_27_out, in_1[2], not_2_out, not_1_out);
  and and_28 (and_28_out, in_1[2], in_1[1], in_1[0]);
  and and_29 (and_29_out, in_1[3], not_3_out, in_1[1], not_1_out);
  or or_2 (a, and_1_out, and_2_out, and_3_out, and_4_out);
  or or_3 (b, and_5_out, and_6_out, and_7_out, and_8_out, and_9_out);
  or or_4 (c, and_10_out, and_11_out, and_12_out, and_13_out, and_14_out);
  or or_5 (or_5_out, and_15_out, and_16_out, and_17_out);
  or or_6 (d, or_5_out, or_7_out);
  or or_7 (or_7_out, and_18_out, and_19_out, and_20_out);
  or or_8 (out_7, and_21_out, and_22_out, and_23_out, and_24_out);
  or or_9 (out_8, and_25_out, and_26_out, and_27_out, and_28_out, and_29_out);

  // Notes on the sheet:
  //   a
  //   b
  //   e
  //   f
  //   g
endmodule
